# Fritzing sketch FritzingSchematics (saved by Fritzing 0.9.3b)
circuit board: 8.46667cm x 5.64444cm

parts:
  Uno_Part = Arduino Uno (Rev3) - ICSP
  Moisture_Sensor = Soil Moisture Sensor
  M1 = DC Motor

nets:
  N1: Uno_Part.A0, Moisture_Sensor.SIG
  5V: Uno_Part.5V, Moisture_Sensor.VCC
  GND: Uno_Part.GND, Moisture_Sensor.GND, M1.pin_2
  N2: Uno_Part.D4, M1.pin_1

notes:
  Shows soil moisture sensor connection
  Used a motor in palce of the pump
